# Fritzing sketch Schematic MK2 (saved by Fritzing 0.9.2b)
perfboards: 1

parts:
  WeMos_D1_Mini1 = WeMos D1 Mini
  U1 = Header 8 [package=1x08_smd]
  U2 = Header 8 [package=1x08_smd]
  DS1 = DS18B20 1-Wire Temperature Sensor [part_number=DS18B20]
  R1 = Resistor [tolerance=±5% resistance=4.7k package="0603 [SMD]"]
  LED1 = LED - 3mm [color="Red (633nm)" package="3 mm [THT]"]
  LED2 = LED - 3mm [color="Green (555nm)" package="3 mm [THT]"]
  R2 = Resistor [tolerance=±5% resistance=1k package="0603 [SMD]"]

nets:
  N1: WeMos_D1_Mini1.D6, LED1.anode
  N2: WeMos_D1_Mini1.G, R2.Pin_0
  N3: U1.1, DS1.VDD, R1.Pin_0
  N4: U1.2, LED2.anode
  N5: U2.2, DS1.GND
  N6: U2.3, DS1.DQ, R1.Pin_1
  N7: LED1.cathode, LED2.cathode

custom parts:
  WeMos D1 Mini: The D1 mini is a mini wifi board based on ESP-8266EX.
